// Logisim project 1011D检测.circ as structural Verilog: 1 circuit, main circuit main
module main (
  input  x,
  output Q2,
  output Q1,
  output Q0,
  output Z
);

  wire and_1_out, and_2_out, and_3_out, and_4_out, CLK_out, D0_qn, D2_qn, nand_1_out, not_1_out, or_1_out;

  Clock #(.highDuration(1), .lowDuration(1)) CLK (.out(CLK_out));
  and and_1 (and_1_out, x, Q0, Q1, D2_qn);
  D_Flip_Flop #(.trigger("rising"), .Pre_Clr_Positions("ABOVE_BELOW"), .NegatePresetClear("false"), .enable("false"), .NewFFLayout("true")) D2 (
    .clk(CLK_out), .D(and_1_out), .Q(Q2), .Qn(D2_qn), .reset(1'b0));  // open: preset
  and and_2 (and_2_out, D2_qn, Q0, not_1_out);
  not not_1 (not_1_out, x);
  D_Flip_Flop #(.trigger("rising"), .Pre_Clr_Positions("ABOVE_BELOW"), .NegatePresetClear("false"), .enable("false"), .NewFFLayout("true")) D1 (
    .clk(CLK_out), .D(or_1_out), .Q(Q1), .reset(1'b0));  // open: Qn, preset
  or or_1 (or_1_out, and_2_out, and_3_out);
  and and_3 (and_3_out, D2_qn, x, D0_qn, Q1);
  and and_4 (and_4_out, x, nand_1_out);
  nand nand_1 (nand_1_out, D2_qn, Q1, Q0);
  D_Flip_Flop #(.trigger("rising"), .Pre_Clr_Positions("ABOVE_BELOW"), .NegatePresetClear("false"), .enable("false"), .NewFFLayout("true")) D0 (
    .clk(CLK_out), .D(and_4_out), .Q(Q0), .Qn(D0_qn), .reset(1'b0));  // open: preset

  assign Z = Q2;
endmodule
