// Logisim project 1011JK检测.circ as structural Verilog: 1 circuit, main circuit main
module main (
  input  x,
  output Q1,
  output Q0,
  output Z
);

  wire and_1_out, and_2_out, and_3_out, CLK_out, j_k_ff_1_qn, j_k_ff_2_qn, not_1_out, or_1_out;

  Clock #(.highDuration(1), .lowDuration(1)) CLK (.out(CLK_out));
  and and_1 (and_1_out, not_1_out, Q0, j_k_ff_1_qn);
  not not_1 (not_1_out, x);
  or or_1 (or_1_out, and_2_out, and_3_out);
  and and_2 (and_2_out, x, Q0);
  J_K_Flip_Flop #(.trigger("rising"), .Pre_Clr_Positions("ABOVE_BELOW"), .NegatePresetClear("false"), .enable("false"), .NewFFLayout("true")) j_k_ff_1 (
    .J(and_1_out), .clk(CLK_out), .K(or_1_out), .Q(Q1), .Qn(j_k_ff_1_qn), .reset(1'b0));  // open: preset
  and and_3 (and_3_out, not_1_out, j_k_ff_2_qn);
  J_K_Flip_Flop #(.trigger("rising"), .Pre_Clr_Positions("ABOVE_BELOW"), .NegatePresetClear("false"), .enable("false"), .NewFFLayout("true")) j_k_ff_2 (
    .J(x), .clk(CLK_out), .K(not_1_out), .Q(Q0), .Qn(j_k_ff_2_qn), .reset(1'b0));  // open: preset
  and and_4 (Z, Q0, Q1, x);
endmodule
